# Fritzing sketch moisture_sensor_v1 (saved by Fritzing 1.0.2b)
circuit board: 4.751cm x 12.3655cm
breadboards: 1

parts:
  R1 = Resistor [tolerance=±5% power=0.25W resistance=220 package=THT]
  LED1 = LED - 5mm [color="Red (633nm)" current=0.030A package="5 mm [THT]"]
  BAT1 = BC9VPC [package=bc9vpc]
  S1 = Pushbutton [package="[THT]"]
  LED2 = LED - 5mm [color="Red (633nm)" current=0.030A package="5 mm [THT]"]
  LED3 = LED - 5mm [color="Red (633nm)" current=0.030A package="5 mm [THT]"]
  LED4 = LED - 5mm [color="Red (633nm)" current=0.030A package="5 mm [THT]"]
  LED5 = LED - 5mm [color="Red (633nm)" current=0.030A package="5 mm [THT]"]
  R2 = Resistor [tolerance=±5% power=0.25W resistance=220 package=THT]
  R3 = Resistor [tolerance=±5% power=0.25W resistance=220 package=THT]
  R4 = Resistor [tolerance=±5% power=0.25W resistance=220 package=THT]
  R5 = Resistor [tolerance=±5% power=0.25W resistance=220 package=THT]
  R6 = Resistor [tolerance=±5% power=0.25W resistance=10 package=THT]
  M1 = Arduino NANO RP2040 CONNECT with headers
  Capacitive_Soil_Moisture_Sensor1 = DFRobot Capacitive Soil Moisture Sensor V1.0 [part_number=SEN0193]
  J1 = shrouded pin header, 6 pins [form="♂ (shrouded male)"]

nets:
  N1: R1.Pin_0, LED1.cathode
  N2: R1.Pin_1, BAT1.V-, R2.Pin_1, R3.Pin_1, R4.Pin_1, R5.Pin_1, R6.Pin_1, M1.GND-4, M1.GND-29, J1.pin4
  N3: LED1.anode, M1.D2
  N4: BAT1.V+, M1.VIN
  N5: S1.Pin_2, M1.+5V
  N6: S1.Pin_3, S1.Pin_4, R6.Pin_0, M1.D10
  N7: LED2.cathode, R2.Pin_0
  N8: LED2.anode, M1.D3
  N9: LED3.cathode, R3.Pin_0
  N10: LED3.anode, M1.D4
  N11: LED4.cathode, R4.Pin_0
  N12: LED4.anode, M1.D5
  N13: LED5.cathode, R5.Pin_0
  N14: LED5.anode, M1.D6
  N15: M1.AREF, Capacitive_Soil_Moisture_Sensor1.A

notes:
  superman_ha_muerto

custom parts:
  DFRobot Capacitive Soil Moisture Sensor V1.0: DFRobot Capacitive Soil Moisture Sensor V1.0 This product measures soil moisture levels by capacitive sensing, rather than resistive sensing like other types of moisture sensor. It is made of a corrosion resistant material giving it a long service life. Insert it into soil and impress your friends with the real-time soil moisture data! The product includes an on-board voltage regulator which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

// code stored in the sketch: moisture_sensor.ino

/*
 * moisture_sensor.ino
 */

 #include <math.h>

#define MOISTURE_SENSOR A0
#define DRY_VALUE 570
#define WET_VALUE 300

#define LED1 2
#define LED2 3
#define LED3 4
#define LED4 5
#define LED5 6

int leds[] = {LED1, LED2, LED3, LED4, LED5};
int numLeds = sizeof(leds) / sizeof(int);


void initLedArray(){
  for( int i = 0; i < numLeds; i++){
    pinMode( leds[i], OUTPUT );
    Serial.println( leds[i], DEC );
  }
}

void setLedArray( int val ){
  for( int i = 0; i < numLeds; i++ ){
    if( i <= val ){
      digitalWrite( leds[i], HIGH );
    }else{
      digitalWrite( leds[i], LOW );
    }
  }
}

/*
 * Converts an analog reading into a integer value (for use in a led scale, for instance)
 *
 * It will apply the formula: 
 *       /                                                           \
 *       |              /    (reading - lowValue)                   \|
 * round |outputRange - | -------------------------- * outputRange  ||
 *       |              \    (DRY_VALUE - lowValue)                 /|
 *       \                                                           /
 *
 *
 */
int convertMoistureReading( int reading, int outputRange ){

  return round( outputRange - ( (reading - WET_VALUE ) / (DRY_VALUE - WET_VALUE) ) * outputRange );

}

void setup() {
  Serial.begin(9600);
  pinMode(LED_BUILTIN, OUTPUT);
  initLedArray();
}

void loop() {
  int moistureReading = analogRead(MOISTURE_SENSOR);
  
  // Print the value to the serial monitor
  Serial.print("Analog output: ");
  Serial.println(moistureReading, DEC);

  digitalWrite(LED_BUILTIN, HIGH);
  setLedArray( convertMoistureReading( moistureReading, numLeds ) );
  delay(1500);
  setLedArray( -1 );
  delay(1500);
  Serial.println("continuamos");
}
